// Digital circuit and.dig as structural Verilog
module \and  (
);

  Switch #(.switchActsAsInput("true")) switch1 ();  // open: A, B
  Switch #(.switchActsAsInput("true")) switch2 ();  // open: A, B
  // PolarityAwareLED LED: pin names not known; wires that end beside it: 1'b1, 1'b0
endmodule
